# Fritzing sketch watering_control (saved by Fritzing 0.9.3b)
breadboards: 1

parts:
  WEMOS = WeMos D1 Mini
  MCP = MCP3008 [package=dil16]
  R1 = Resistor [tolerance=±5% resistance=330 package=THT]
  R2 = Resistor [tolerance=±5% resistance=330 package=THT]
  R3 = Resistor [tolerance=±5% resistance=330 package=THT]
  R4 = Resistor [tolerance=±5% resistance=330 package=THT]
  TIP120 = TRANSISTOR_NPN [package=sot223]
  TIP120_2 = TRANSISTOR_NPN [package=sot223]
  TIP120_3 = TRANSISTOR_NPN [package=sot223]
  V1 = DC Power [voltage=12V]
  U1 = Hirose DF13 Series Header [part_number=PUMP_3 package=DF13C-2P-1.25V]
  U2 = Hirose DF13 Series Header [part_number=PUMP_2 package=DF13C-2P-1.25V]
  U3 = Hirose DF13 Series Header [part_number=PUMP_4 package=DF13C-2P-1.25V]
  P1 = Hirose DF13 Series Header [part_number=PUMP_1 package=DF13C-2P-1.25V]
  D8 = Rectifier Diode [part_number=1N4001 package="300 mil [THT]"]
  D9 = Rectifier Diode [part_number=1N4001 package="300 mil [THT]"]
  D10 = Rectifier Diode [part_number=1N4001 package="300 mil [THT]"]
  D11 = Rectifier Diode [part_number=1N4001 package="300 mil [THT]"]
  D12 = Rectifier Diode [part_number=1N4001 package="300 mil [THT]"]
  TIP120_4 = TRANSISTOR_NPN [package=sot223]
  7805 = Voltage Regulator [package=to220-igo]
  100µF = Electrolytic Capacitor [package="2cm H-Type"]
  100µF_2 = Electrolytic Capacitor [package="2cm H-Type"]
  U4 = Hirose DF13 Series Header [part_number=SENSOR_7 package=DF13C-3P-1.25V]
  U5 = Hirose DF13 Series Header [part_number=SENSOR_4 package=DF13C-3P-1.25V]
  U6 = Hirose DF13 Series Header [part_number=SENSOR_5 package=DF13C-3P-1.25V]
  U7 = Hirose DF13 Series Header [part_number=SENSOR_3 package=DF13C-3P-1.25V]
  U8 = Hirose DF13 Series Header [part_number=SENSOR_6 package=DF13C-3P-1.25V]
  U9 = Hirose DF13 Series Header [part_number=SENSOR_8 package=DF13C-3P-1.25V]
  U10 = Hirose DF13 Series Header [part_number=SENSOR_1 package=DF13C-3P-1.25V]
  U11 = Hirose DF13 Series Header [part_number=SENSOR_2 package=DF13C-3P-1.25V]

nets:
  3V3: WEMOS.3V3, MCP.VDD
  N1: WEMOS.5V, 7805.OUT, 100µF_2.+
  N2: WEMOS.D0, R4.Pin_0
  N3: WEMOS.D1, R2.Pin_0
  N4: WEMOS.D2, R1.Pin_0
  N5: WEMOS.D3, R3.Pin_0
  N6: WEMOS.D5, MCP.CLK
  N7: WEMOS.D6, MCP.Dout
  N8: WEMOS.D7, MCP.Din
  N9: WEMOS.D8, MCP.CS/SHDN
  N10: WEMOS.G, TIP120.E, TIP120_2.E, TIP120_3.E, V1.V-, TIP120_4.E, 7805.GND, 100µF.-, 100µF_2.-, U4.1, U5.1, U6.1, U7.1, U8.1, U9.1, U10.1, U11.1
  N11: MCP.CH0, U10.3
  N12: MCP.CH1, U11.3
  N13: MCP.CH2, U7.3
  N14: MCP.CH3, U5.3
  N15: MCP.CH4, U6.3
  N16: MCP.CH5, U8.3
  N17: MCP.CH6, U4.3
  N18: MCP.CH7, U9.3
  N19: MCP.DGND, MCP.AGND
  N20: MCP.VREF, U4.2, U5.2, U6.2, U7.2, U8.2, U9.2, U10.2, U11.2
  N21: R1.Pin_1, TIP120_2.B
  N22: R2.Pin_1, TIP120.B
  N23: R3.Pin_1, TIP120_3.B
  N24: R4.Pin_1, TIP120_4.B
  N25: TIP120.C, U2.1, D8.anode
  N26: TIP120_2.C, U1.1, D10.anode
  N27: TIP120_3.C, U3.1, D11.anode
  N28: V1.V+, D12.anode
  N29: U1.2, U2.2, U3.2, P1.2, D8.cathode, D9.cathode, D10.cathode, D11.cathode, D12.cathode, 7805.IN, 100µF.+
  N30: P1.1, D9.anode, TIP120_4.C
