# Fritzing sketch watering_array (saved by Fritzing 0.9.3b)
breadboards: 1

parts:
  WEMOS = WeMos D1 Mini
  R4 = Resistor [tolerance=±5% resistance=330 package=THT]
  V1 = DC Power [voltage=5V]
  P1 = Hirose DF13 Series Header [part_number=PUMP package=DF13C-2P-1.25V]
  D9 = Rectifier Diode [part_number=1N4001 package="300 mil [THT]"]
  TIP120 = TRANSISTOR_NPN [package=sot223]
  U11 = Hirose DF13 Series Header [part_number="SENSOR (analogl)" package=DF13C-3P-1.25V]
  U12 = Hirose DF13 Series Header [part_number="LED (green / red)" package=DF13C-3P-1.25V]
  R7 = Resistor [tolerance=±5% resistance=470 package=THT]
  R8 = Resistor [tolerance=±5% resistance=470 package=THT]
  U13 = Hirose DF13 Series Header [part_number="ON / OFF" package=DF13C-2P-1.25V]
  U10 = Hirose DF13 Series Header [part_number="SENSOR (digital)" package=DF13C-2P-1.25V]
  R9 = Resistor [tolerance=±5% resistance=10k package=THT]
  R11 = Trimmer Potentiometer [maximum_resistance=10kΩ package=THT]
  JP1 = Jumper [part_number=RESET_JUMPER package=sj_2s-no]

nets:
  N1: WEMOS.3V3, U11.1, U10.1
  N2: WEMOS.5V, V1.V+, P1.2, D9.cathode
  N3: WEMOS.A0, R11.wiper
  N4: WEMOS.D0, JP1.1
  N5: WEMOS.D5, U10.2, R9.Pin_0
  N6: WEMOS.D6, R7.Pin_0
  N7: WEMOS.D7, R8.Pin_0
  N8: WEMOS.D8, R4.Pin_0
  N9: WEMOS.G, TIP120.E, U11.2, U12.2, U13.1, R9.Pin_1, R11.leg1
  N10: WEMOS.RST, JP1.2
  N11: R4.Pin_1, TIP120.B
  N12: V1.V-, U13.2
  N13: P1.1, D9.anode, TIP120.C
  N14: U11.3, R11.leg2
  N15: U12.1, R8.Pin_1
  N16: U12.3, R7.Pin_1

// code stored in the sketch: Untitled.ino

